# Fritzing sketch Catan-schematic-diagram (saved by Fritzing 1.0.1rc)

parts:
  Part1 = Arduino Nano (Rev3.0)
  VCC1 = Battery block 9V
  C1 = Capacitor Polarized [package=cpol-radial-1000uf-25v]
  S1 = Pushbutton [package="[THT]"]
  R1 = Resistor [tolerance=±5% resistance=220 package="0805 [SMD]"]
  R2 = Resistor [tolerance=±5% resistance=220 package="0805 [SMD]"]
  Grove1 = Grove 4 Digit Display
  Grove2 = Grove OLED 128x96
  RGB_SMD_LED1 = SMD RGB LED (WS2812) [package=5050]
  RGB_SMD_LED2 = SMD RGB LED (WS2812) [package=5050]  # not connected
  RGB_SMD_LED3 = SMD RGB LED (WS2812) [package=5050]  # not connected
  RGB_SMD_LED4 = SMD RGB LED (WS2812) [package=5050]
  RGB_SMD_LED5 = SMD RGB LED (WS2812) [package=5050]
  RGB_SMD_LED6 = SMD RGB LED (WS2812) [package=5050]  # not connected
  RGB_SMD_LED7 = SMD RGB LED (WS2812) [package=5050]  # not connected
  RGB_SMD_LED8 = SMD RGB LED (WS2812) [package=5050]
  RGB_SMD_LED9 = SMD RGB LED (WS2812) [package=5050]

nets:
  N1: Part1.D2, Grove1.CLK
  N2: Part1.D3, Grove1.DIO
  N3: Part1.D4, R2.Pin_0
  N4: Part1.D5, S1.Pin_1
  N5: Part1.VIN, VCC1.+
  GND: Part1.GND, VCC1.-, C1.-, Grove2.GND, RGB_SMD_LED1.DOut
  VCC: Part1.5V, C1.+, Grove2.VCC, RGB_SMD_LED1.VCC
  N6: Part1.A5, Grove2.SDA
  N7: Part1.A4, Grove2.SCL
  N8: S1.Pin_4, Grove1.GND
  N9: R1.Pin_0, Grove1.VCC
  N10: R2.Pin_1, RGB_SMD_LED1.DIn
  N11: RGB_SMD_LED4.NC, RGB_SMD_LED5.VCC
  N12: RGB_SMD_LED4.VDD, RGB_SMD_LED5.DIn
  N13: RGB_SMD_LED4.VSS, RGB_SMD_LED5.DOut
  N14: RGB_SMD_LED8.NC, RGB_SMD_LED9.VCC
  N15: RGB_SMD_LED8.VDD, RGB_SMD_LED9.DIn

notes:
  81 LEDs
